# Fritzing sketch Schematic (saved by Fritzing 0.9.3b)

parts:
  Raspberry_Pi_1 = Raspberry Pi 3 [part_number=RPI-3-V1.2]
  S1 = Round Pushbutton
  S2 = Round Pushbutton
  S3 = Round Pushbutton
  S4 = Round Pushbutton
  S5 = Round Pushbutton

nets:
  N1: Raspberry_Pi_1.GIPO17, S1.leg0
  N2: Raspberry_Pi_1.GIPO27, S5.leg0
  N3: Raspberry_Pi_1.GIPO22, S2.leg0
  N4: Raspberry_Pi_1.GIPO24, S4.leg0
  N5: Raspberry_Pi_1.GIPO23, S3.leg0
  N6: Raspberry_Pi_1.GND, S1.leg1

notes:
  button_1
  BUTTON_2
  BUTTON_4
  BUTTON_3
  BUTTON_5
